# Fritzing sketch Schéma du circuit (saved by Fritzing 0.9.2b)
breadboards: 1

parts:
  Raspberry_Pi1 = Raspberry Pi 2
  LED1 = smd LED [color="Red (633nm)" package="0603 [SMD]"]
  R1 = Resistor [tolerance=±5% resistance=220 package="2010 [SMD]"]
  J1 = Infrared Proximity Sensor
  R2 = Resistor [tolerance=±5% resistance=220 package="2010 [SMD]"]
  LED2 = smd LED [color="Yellow (595nm)" package="0603 [SMD]"]
  R3 = Resistor [tolerance=±5% resistance=220 package="2010 [SMD]"]
  LED3 = smd LED [color="Red (633nm)" package="0603 [SMD]"]
  R4 = Resistor [tolerance=±5% resistance=220 package="2010 [SMD]"]
  LED4 = smd LED [color="Green (555nm)" package="0603 [SMD]"]

nets:
  N1: Raspberry_Pi1.GPIO24, LED4.anode
  N2: Raspberry_Pi1.GPIO23, LED3.anode
  N3: Raspberry_Pi1.GPIO18, LED2.anode
  GND: Raspberry_Pi1.GND, R1.Pin_0, J1.GND, R2.Pin_0, R3.Pin_0
  5V: Raspberry_Pi1.5V, LED1.anode, J1.Vcc
  N4: LED1.cathode, R1.Pin_1
  N5: R2.Pin_1, LED2.cathode
  N6: R3.Pin_1, LED3.cathode
  N7: R4.Pin_1, LED4.cathode
